# Fritzing sketch esp-rsc (saved by Fritzing 0.9.3b)
perfboards: 1

parts:
  U1 = ESP32-38PinWide [part_number=ESP32-38PinWide]
  J1 = female pin header, 2 pins [form="♀ (female)"]
  J2 = female pin header, 2 pins [form="♀ (female)"]
  J3 = female pin header, 2 pins [form="♀ (female)"]
  J4 = female pin header, 2 pins [form="♀ (female)"]
  J5 = female pin header, 2 pins [form="♀ (female)"]
  R2 = Resistor [tolerance=±5% resistance=10k package=THT]
  R3 = Resistor [tolerance=±5% resistance=10k package=THT]
  R4 = Resistor [tolerance=±5% resistance=10k package=THT]
  R5 = Resistor [tolerance=±5% resistance=10k package=THT]
  R6 = Resistor [tolerance=±5% resistance=10k package=THT]
  U2 = Sharp PC817 [package=THT]
  U3 = Sharp PC817 [package=THT]
  U4 = Sharp PC817 [package=THT]
  J6 = female pin header, 8 pins [form="♀ (female)"]
  R7 = Resistor [tolerance=±5% resistance=10k package=THT]
  R8 = Resistor [tolerance=±5% resistance=10k package=THT]
  R9 = Resistor [tolerance=±5% resistance=10k package=THT]
  J7 = female pin header, 8 pins [form="♀ (female)"]
  R10 = Resistor [tolerance=±5% resistance=330 package=THT]
  R13 = Resistor [tolerance=±5% resistance=330 package=THT]
  R14 = Resistor [tolerance=±5% resistance=330 package=THT]
  R15 = Resistor [tolerance=±5% resistance=330 package=THT]
  R16 = Resistor [tolerance=±5% resistance=330 package=THT]
  J8 = female pin header, 8 pins [form="♀ (female)"]

nets:
  N1: U1.3.3, U2.Pin_4
  N2: U1.GPIO34, J5.pin2, R6.Pin_0
  N3: U1.GPIO35, J4.pin2, R5.Pin_0
  N4: U1.GPIO32, J3.pin2, R4.Pin_0
  N5: U1.GPIO33, J2.pin2, R3.Pin_0
  N6: U1.GPIO25, J1.pin2, R2.Pin_0
  N7: U1.GND, R8.Pin_0, J7.pin8
  N8: U1.GPIO11, J5.pin1
  N9: U1.GPIO4, U2.Pin_3
  N10: U1.GPIO16, R16.Pin_1
  N11: U1.GPIO17, R13.Pin_1
  N12: U1.GPIO18, U4.Pin_1
  N13: U1.GPIO19, U3.Pin_1
  N14: U1.GPIO21, R14.Pin_1
  N15: U1.GPIO22, R15.Pin_1
  N16: U1.GPIO23, R10.Pin_1
  N17: R2.Pin_1, R6.Pin_1
  N18: U2.Pin_1, J6.pin8
  N19: U2.Pin_2, R7.Pin_1
  N20: U3.Pin_2, R8.Pin_1
  N21: U3.Pin_4, J6.pin4, J7.pin4
  N22: U3.Pin_3, J6.pin3, J7.pin3
  N23: U4.Pin_2, R9.Pin_1
  N24: U4.Pin_4, J6.pin1, J7.pin1
  N25: U4.Pin_3, J6.pin2, J7.pin2
  N26: J6.pin5, J7.pin5
  N27: J6.pin6, J7.pin6
  N28: J6.pin7, R7.Pin_0
  N29: J7.pin7, R10.Pin_0
  N30: R13.Pin_0, J8.pin4
  N31: R14.Pin_0, J8.pin6
  N32: R15.Pin_0, J8.pin8
  N33: R16.Pin_0, J8.pin2

notes:
  4 - Power Led (INPUT_PULLUP)
  18 - Power Button (OUTPUT)
  19 - Reset Button (OUTPUT)
  23 - Power Led Simulator (OUTPUT)
  22 - LED01 (OUTPUT)
  21 - LED02 (OUTPUT)
  17 - LED03 (OUTPUT)
  16 - LED-ALERT (OUTPUT)
  25 - CPU (INPUT)
  26 - PSU (INPUT)
  32 - NIC (INPUT)
  33 - RAID (INPUT)
  34 - EXP (INPUT)
  ALT TARAF - ANAKART
  ÜST TARAF - KASA

custom parts:
  ESP32-38PinWide: Generic 38-Pin ESP32 with wide format (only access to one side of pins on a breadboard) based on Stephen Lilley's HiLetgo ESP-WROOM-32 ESP32 ESP-32S Development Board.
